// Logisim project satanja.circ as structural Verilog
module ALU (
);

  wire [7:0] arithmetriclogic_1_o;

  ArithmetricLogic arithmetriclogic_1 (.O(arithmetriclogic_1_o));  // open: A, Ia, B, Io, Be, Ib, N, X, Ci, Co
  Shiftre shiftre_1 (.I(arithmetriclogic_1_o));  // open: E, R, L, O_r, O, O_l
endmodule

module ArithmetricLogic (
  input  [7:0] A,
  input  Ia,
  input  [7:0] B,
  input  Io,
  input  Be,
  input  Ib,
  input  N,
  input  X,
  input  Ci,
  output [7:0] O,
  output Co
);

  wire arithmetriclogicbit_2_co, arithmetriclogicbit_3_co, arithmetriclogicbit_4_co,
       arithmetriclogicbit_5_co, arithmetriclogicbit_6_co, arithmetriclogicbit_7_co, arithmetriclogicbit_8_co;
  wire [7:0] and_1_out, and_2_out, arithmetriclogicbit_8_o, or_1_out, xor_1_out;

  assign xor_1_out = A ^ {8{Ia}};  // XOR_Gate xor_1, 8 bits wide
  assign and_1_out = B & {8{Be}};  // AND_Gate and_1, 8 bits wide
  assign or_1_out = and_1_out | and_2_out;  // OR_Gate or_1, 8 bits wide
  assign and_2_out = ~B & {8{Ib}};  // AND_Gate and_2, 8 bits wide
  ArithmetricLogicBit arithmetriclogicbit_1 (
    .A(xor_1_out[7]), .B(or_1_out[7]), .Ci(arithmetriclogicbit_2_co), .N(N), .X(X), .Co(Co),
    .O(arithmetriclogicbit_8_o[7]));
  ArithmetricLogicBit arithmetriclogicbit_2 (
    .A(xor_1_out[6]), .B(or_1_out[6]), .Ci(arithmetriclogicbit_3_co), .N(N), .X(X),
    .Co(arithmetriclogicbit_2_co), .O(arithmetriclogicbit_8_o[6]));
  ArithmetricLogicBit arithmetriclogicbit_3 (
    .A(xor_1_out[5]), .B(or_1_out[5]), .Ci(arithmetriclogicbit_4_co), .N(N), .X(X),
    .Co(arithmetriclogicbit_3_co), .O(arithmetriclogicbit_8_o[5]));
  ArithmetricLogicBit arithmetriclogicbit_4 (
    .A(xor_1_out[4]), .B(or_1_out[4]), .Ci(arithmetriclogicbit_5_co), .N(N), .X(X),
    .Co(arithmetriclogicbit_4_co), .O(arithmetriclogicbit_8_o[4]));
  ArithmetricLogicBit arithmetriclogicbit_5 (
    .A(xor_1_out[3]), .B(or_1_out[3]), .Ci(arithmetriclogicbit_6_co), .N(N), .X(X),
    .Co(arithmetriclogicbit_5_co), .O(arithmetriclogicbit_8_o[3]));
  ArithmetricLogicBit arithmetriclogicbit_6 (
    .A(xor_1_out[2]), .B(or_1_out[2]), .Ci(arithmetriclogicbit_7_co), .N(N), .X(X),
    .Co(arithmetriclogicbit_6_co), .O(arithmetriclogicbit_8_o[2]));
  ArithmetricLogicBit arithmetriclogicbit_7 (
    .A(xor_1_out[1]), .B(or_1_out[1]), .Ci(arithmetriclogicbit_8_co), .N(N), .X(X),
    .Co(arithmetriclogicbit_7_co), .O(arithmetriclogicbit_8_o[1]));
  ArithmetricLogicBit arithmetriclogicbit_8 (
    .A(xor_1_out[0]), .B(or_1_out[0]), .Ci(Ci), .N(N), .X(X), .Co(arithmetriclogicbit_8_co),
    .O(arithmetriclogicbit_8_o[0]));
  assign O = {8{Io}} ^ arithmetriclogicbit_8_o;  // XOR_Gate xor_2, 8 bits wide
endmodule

module ArithmetricLogicBit (
  input  A,
  input  B,
  input  Ci,
  input  N,
  input  X,
  output Co,
  output O
);

  wire and_1_out, and_2_out, and_3_out, and_4_out, and_5_out, and_6_out, and_7_out, xor_1_out, xor_2_out;

  and and_1 (and_1_out, A, B);
  xor xor_1 (xor_1_out, A, B);
  and and_2 (and_2_out, and_1_out, N, ~X);  // AND_Gate
  and and_3 (and_3_out, and_1_out, ~N, ~X);  // AND_Gate
  and and_4 (and_4_out, xor_1_out, ~N, X);  // AND_Gate
  and and_5 (and_5_out, xor_1_out, ~N, ~X);  // AND_Gate
  and and_6 (and_6_out, Ci, ~N, ~X);  // AND_Gate
  and and_7 (and_7_out, and_6_out, and_5_out);
  xor xor_2 (xor_2_out, and_6_out, and_5_out);
  or or_1 (Co, and_3_out, and_7_out);
  or or_2 (O, and_2_out, and_4_out, xor_2_out);
endmodule

module Shiftre (
  input  [7:0] I,
  input  E,
  input  R,
  input  L,
  output O_r,
  output [7:0] O,
  output O_l
);

  wire and_1_out, and_2_out, and_4_out, and_5_out, and_6_out, and_7_out, and_8_out, and_9_out, and_10_out,
       and_11_out, and_12_out, and_13_out, and_14_out, and_15_out, and_16_out, and_17_out, and_18_out,
       and_19_out, and_20_out, and_21_out, and_22_out, and_23_out, and_24_out, and_25_out, and_26_out,
       not_1_out;

  not not_1 (not_1_out, E);
  and and_1 (and_1_out, E, ~R);  // AND_Gate
  and and_2 (and_2_out, E, R);
  and and_3 (O_r, I[0], and_2_out);
  and and_4 (and_4_out, I[0], not_1_out);
  and and_5 (and_5_out, I[0], and_1_out);
  and and_6 (and_6_out, I[1], and_2_out);
  and and_7 (and_7_out, I[1], not_1_out);
  and and_8 (and_8_out, I[1], and_1_out);
  and and_9 (and_9_out, I[2], and_2_out);
  and and_10 (and_10_out, I[2], not_1_out);
  and and_11 (and_11_out, I[2], and_1_out);
  and and_12 (and_12_out, I[3], and_2_out);
  and and_13 (and_13_out, I[3], not_1_out);
  and and_14 (and_14_out, I[3], and_1_out);
  and and_15 (and_15_out, I[4], and_2_out);
  and and_16 (and_16_out, I[4], not_1_out);
  and and_17 (and_17_out, I[4], and_1_out);
  and and_18 (and_18_out, I[5], and_2_out);
  and and_19 (and_19_out, I[5], not_1_out);
  and and_20 (and_20_out, I[5], and_1_out);
  and and_21 (and_21_out, I[6], and_2_out);
  and and_22 (and_22_out, I[6], not_1_out);
  and and_23 (and_23_out, I[6], and_1_out);
  and and_24 (and_24_out, I[7], and_2_out);
  and and_25 (and_25_out, I[7], not_1_out);
  and and_26 (and_26_out, I[7], R, L);
  and and_27 (O_l, I[7], and_1_out);
  or or_1 (O[0], and_4_out, and_6_out);
  or or_2 (O[1], and_5_out, and_7_out, and_9_out);
  or or_3 (O[2], and_8_out, and_10_out, and_12_out);
  or or_4 (O[3], and_11_out, and_13_out, and_15_out);
  or or_5 (O[4], and_14_out, and_16_out, and_18_out);
  or or_6 (O[5], and_17_out, and_19_out, and_21_out);
  or or_7 (O[6], and_20_out, and_22_out, and_24_out);
  or or_8 (O[7], and_23_out, and_25_out, and_26_out);
endmodule
